// Logisim project Aufgabe2.circ as structural Verilog: 3 circuits, main circuit Distrunktive NF
module Distrunktive_NF (
  input  in_1,
  input  in_2,
  input  in_3,
  output out_4
);

  wire and_1_out, and_2_out, and_3_out, and_4_out;

  and and_1 (and_1_out, ~in_1, ~in_2, in_3);  // AND_Gate
  and and_2 (and_2_out, ~in_1, in_2, ~in_3);  // AND_Gate
  and and_3 (and_3_out, ~in_1, ~in_2, in_3);  // AND_Gate
  and and_4 (and_4_out, in_1, in_2, in_3);
  or or_1 (out_4, and_1_out, and_2_out, and_3_out, and_4_out);
endmodule

module FlipFlop (
  input  in_1,
  input  in_2,
  input  in_3,
  input  in_4,
  output out_5
);

  wire clock_1_out, or_1_out;

  Clock clock_1 (.out(clock_1_out));
  or or_1 (or_1_out, in_1, in_2, in_3, in_4);
  T_Flip_Flop t_ff_1 (.clk(or_1_out), .T(clock_1_out), .Q(out_5));  // open: Qn, preset, reset, en
endmodule

module Konjunktive_NF (
  input  in_1,
  input  in_2,
  input  in_3,
  output out_4
);

  wire or_1_out, or_2_out, or_3_out, or_4_out;

  or or_1 (or_1_out, in_1, in_2, in_3);
  or or_2 (or_2_out, in_1, ~in_2, ~in_3);  // OR_Gate
  or or_3 (or_3_out, ~in_1, in_2, ~in_3);  // OR_Gate
  or or_4 (or_4_out, ~in_1, ~in_2, in_3);  // OR_Gate
  and and_1 (out_4, or_1_out, or_2_out, or_3_out, or_4_out);
endmodule
