// Logisim project Aufgabe3.circ as structural Verilog: 2 circuits, main circuit distrunktive NF
module distrunktive_NF (
  input  in_1,
  input  in_2,
  input  in_3,
  output out_4
);

  wire and_1_out, and_2_out, and_3_out, and_4_out, and_5_out;

  and and_1 (and_1_out, ~in_1, in_2, in_3);  // AND_Gate
  and and_2 (and_2_out, in_1, ~in_2, ~in_3);  // AND_Gate
  and and_3 (and_3_out, in_1, ~in_2, in_3);  // AND_Gate
  and and_4 (and_4_out, in_1, in_2, ~in_3);  // AND_Gate
  and and_5 (and_5_out, in_1, in_2, in_3);
  or or_1 (out_4, and_1_out, and_2_out, and_3_out, and_4_out, and_5_out);
endmodule

module konjunktive_NF (
  input  in_1,
  input  in_2,
  input  in_3,
  output out_4
);

  wire or_1_out, or_2_out, or_3_out;

  or or_1 (or_1_out, in_1, in_2, in_3);
  or or_2 (or_2_out, in_1, in_2, ~in_3);  // OR_Gate
  or or_3 (or_3_out, in_1, ~in_2, in_3);  // OR_Gate
  and and_1 (out_4, or_1_out, or_2_out, or_3_out);
endmodule
